# Fritzing sketch BTS7960 Connection System (saved by Fritzing 0.9.3b)
stripboards: 3

parts:
  M1 = BTS7960 [part_number=BTS7960(IC0)]
  M2 = BTS7960 [part_number=BTS7960(IC1)]
  M3 = BTS7960 [part_number=BTS7960(IC3)]
  M4 = BTS7960 [part_number=BTS7960(IC2)]
  U1 = 4053 [part_number=74HC4053(IC0) package="DIP (Dual Inline) [THT]"]
  Εξάρτημα1 = 4053 [package="DIP (Dual Inline) [THT]"]  # not connected
  U1_1 = 4053 [package="DIP (Dual Inline) [THT]"]  # not connected
  U1_2 = 4053 [package="DIP (Dual Inline) [THT]"]  # not connected
  U1_3 = 4053 [package="DIP (Dual Inline) [THT]"]  # not connected
  IC1 = MCP23017 I2C I/O Expander [part_number=MCP23S17(IC0)]
  Raspberry_Pi1 = Raspberry Pi B+
  U2 = 4053 [part_number=74HC4053(IC1) package="DIP (Dual Inline) [THT]"]
  U2_3 = 4053 [package="DIP (Dual Inline) [THT]"]  # not connected
  U2_2 = 4053 [package="DIP (Dual Inline) [THT]"]  # not connected
  U2_1 = 4053 [package="DIP (Dual Inline) [THT]"]  # not connected
  part = 4053 [package="DIP (Dual Inline) [THT]"]  # not connected

nets:
  N1: M1.pin1, U1.connector11
  N2: M1.pin2, U1.connector12
  N3: M1.pin3, M1.pin4, M3.pin3, M3.pin4, IC1.GPA3, IC1.GPB4
  N4: M2.pin1, U1.connector1
  N5: M2.pin2, U1.connector0
  N6: M2.pin3, M2.pin4, M4.pin3, M4.pin4, IC1.GPA4, IC1.GPB3
  N7: M3.pin1, U2.connector1
  N8: M3.pin2, U2.connector0
  N9: M4.pin1, U2.connector11
  N10: M4.pin2, U2.connector12
  N11: U1.connector8, IC1.GPA2, IC1.GPB5
  N12: U1.connector9, IC1.GPA1, IC1.GPB6
  N13: U1.connector10, IC1.GPA0, IC1.GPB7
  N14: U1.connector13, Raspberry_Pi1.GPIO13
  N15: U1.connector14, Raspberry_Pi1.GPIO19
  N16: IC1.A0, IC1.SO, Raspberry_Pi1.GPIO9
  N17: IC1.A1, IC1.SI, Raspberry_Pi1.GPIO10
  N18: IC1.A2, IC1.SCK, Raspberry_Pi1.GPIO11
  N19: IC1.RESET, IC1.CS, Raspberry_Pi1.GPIO8
  N20: IC1.INTB, IC1.VSS
  N21: IC1.INTA, IC1.VDD
  N22: IC1.GPA5, IC1.GPB2, U2.connector8
  N23: IC1.GPA6, IC1.GPB1, U2.connector9
  N24: IC1.GPA7, IC1.GPB0, U2.connector10
  N25: Raspberry_Pi1.GPIO12, U2.connector14
  N26: Raspberry_Pi1.GPIO18, U2.connector13

notes:
  24V Power Source
  5V Buck Converter
  TODO
  Βάλε pull-down resistor
  OVERAL TODO
  The mirroring left-right motors motion will be handle in source code at functions like moveForwardFrontLeftMotor(), moveBackwardFrontLeftMotor(), etc for the other 3 motors.

custom parts:
  BTS7960: BTS7960 43A Peak Power H-Bridge PWM Motor Driver
  4053: A 4053 three element single throw double pole analog switch in schematic subpart format.
  4053: A 4053 three element single throw double pole analog switch in schematic subpart format.
  4053: A 4053 three element single throw double pole analog switch in schematic subpart format.
  4053: A 4053 three element single throw double pole analog switch in schematic subpart format.
  4053: A 4053 three element single throw double pole analog switch in schematic subpart format.
  MCP23017 I2C I/O Expander: The MCP23017 uses two i2c pins (these can be shared with other i2c devices), and in exchange gives you 16 general purpose pins. You can set each of 16 pins to be input, output, input with a pullup or open drain. There's even the ability to get an interrupt via an external pin when any of the inputs change so you don't have to keep polling the chip.
